# Fritzing sketch BathroomFan (saved by Fritzing 0.8.0b)
breadboards: 1

parts:
  Arduino1 = Arduino
  DHT1 = DHT22 Humidity and Temperature Sensor
  C1 = Ceramic Capacitor [capacitance=100nF package="100 mil [THT, multilayer]"]
  R1 = 1k Ω Resistor [package=THT]
  K1 = Relay [part_number=FRS1B-S package=THT]
  D3 = Rectifier Diode [part_number=1N4001 package="300 mil [THT]"]
  Q1 = NPN-Transistor [package="TO92 [THT]"]
  R2 = 1k Ω Resistor [package=THT]
  R3 = 10k Ω Resistor [package=THT]

nets:
  GND: Arduino1.GND, DHT1.GND, C1.1, Q1.E, R3.Pin_1
  N1: Arduino1.D8, R2.Pin_0
  N2: Arduino1.D4, DHT1.DATA, R1.Pin_1
  5V: Arduino1.+5V, DHT1.VDD, C1.0, R1.Pin_0, K1.COIL2, D3.cathode
  N3: K1.COIL1, D3.anode, Q1.C
  N4: K1.C1, K1.C2
  N5: Q1.B, R2.Pin_1, R3.Pin_0
